// Logisim project datapath with control unit.circ as structural Verilog: 3 circuits, main circuit main
module main (
  input  in_1,
  output carryOut,
  output overflow
);

  wire clock_1_out, control_unit_1_alusrc, control_unit_1_mem_to_reg, control_unit_1_memory_write,
       control_unit_1_memread, control_unit_1_regdst, control_unit_1_regwrite;
  wire [1:0] control_unit_1_aluop;
  wire [2:0] alu_control_1_operation;
  wire [3:0] multiplexer_1_out;
  wire [7:0] rom_1_data;
  wire [15:0] bit_extender_1_out, multiplexer_2_out, multiplexer_3_out, n16_bit_alu_1_result,
       n16_bit_register_1_read_data_1, n16_bit_register_1_read_data_2, ram_1_data;
  wire [19:0] adder_1_out, register_1_q;
  wire [19:8] rom_1_data_2;

  Clock clock_1 (.out(clock_1_out));
  Register #(.width(20)) register_1 (.D(adder_1_out), .Q(register_1_q), .clk(clock_1_out), .clr(in_1));  // open: en
  assign bit_extender_1_out = {{8{rom_1_data[7]}}, rom_1_data};  // Bit_Extender bit_extender_1
  Adder #(.width(20)) adder_1 (.a(20'h1), .b(register_1_q), .out(adder_1_out));  // open: cin, cout
  ROM #(.addrWidth(20), .dataWidth(20)) rom_1 (.addr(register_1_q), .data({rom_1_data_2, rom_1_data}));  // open: sel
  control_unit control_unit_1 (
    .opcode(rom_1_data_2[19:16]), .regDst(control_unit_1_regdst), .AluSrc(control_unit_1_alusrc),
    .regWrite(control_unit_1_regwrite), .memRead(control_unit_1_memread),
    .mem_to_reg(control_unit_1_mem_to_reg), .memory_write(control_unit_1_memory_write),
    .ALUOp(control_unit_1_aluop));
  Multiplexer #(.width(4)) multiplexer_1 (
    .in0(rom_1_data_2[11:8]), .in1(rom_1_data[7:4]), .out(multiplexer_1_out), .sel(control_unit_1_regdst));  // open: en
  ALu_Control alu_control_1 (
    .\function (rom_1_data[3:0]), .ALUOp(control_unit_1_aluop), .Operation(alu_control_1_operation));
  _16_bit_register u_16_bit_register_1 (
    .write_data(multiplexer_3_out), .Write_register(multiplexer_1_out),
    .read_register_1(rom_1_data_2[15:12]), .read_register_2(rom_1_data_2[11:8]),
    .read_data_1(n16_bit_register_1_read_data_1), .read_data_2(n16_bit_register_1_read_data_2),
    .regWrite(control_unit_1_regwrite), .in_6(clock_1_out));
  Multiplexer #(.width(16)) multiplexer_2 (
    .in0(n16_bit_register_1_read_data_2), .in1(bit_extender_1_out), .out(multiplexer_2_out),
    .sel(control_unit_1_alusrc));  // open: en
  _16_bit_ALU u_16_bit_alu_1 (
    .Operand_A(n16_bit_register_1_read_data_1), .Operand_B(multiplexer_2_out),
    .Operation(alu_control_1_operation[1:0]), .Binvert(alu_control_1_operation[2]),
    .result(n16_bit_alu_1_result), .Carry15(carryOut), .Carry_In(alu_control_1_operation[2]),
    .Overflow(overflow));  // open: zero
  RAM #(.addrWidth(16), .dataWidth(16), .bus("separate")) ram_1 (
    .addr(n16_bit_alu_1_result), .din(n16_bit_register_1_read_data_2), .data(ram_1_data),
    .str(control_unit_1_memory_write), .clk(clock_1_out), .ld(control_unit_1_memread));  // open: sel, clr
  Multiplexer #(.width(16)) multiplexer_3 (
    .in0(n16_bit_alu_1_result), .in1(ram_1_data), .out(multiplexer_3_out), .sel(control_unit_1_mem_to_reg));  // open: en

  // Notes on the sheet:
  //   contents of rom_1 (hex, n*v repeats v):
  //   30101 30202 1232 b0303
endmodule

module control_unit (
  input  [3:0] opcode,
  output regDst,
  output AluSrc,
  output regWrite,
  output memRead,
  output mem_to_reg,
  output memory_write,
  output [1:0] ALUOp
);

  and R_type (ALUOp[1], ~opcode[3], ~opcode[2], ~opcode[1], ~opcode[0]);  // AND_Gate
  and lw (mem_to_reg, ~opcode[3], ~opcode[2], opcode[1], opcode[0]);  // AND_Gate
  and sw (memory_write, opcode[3], ~opcode[2], opcode[1], opcode[0]);  // AND_Gate
  or or_1 (AluSrc, mem_to_reg, memory_write);
  or or_2 (regWrite, ALUOp[1], mem_to_reg);

  assign ALUOp[0] = 1'b0;
  assign memRead = mem_to_reg;
  assign regDst = ALUOp[1];
endmodule

// ALU control
module ALu_Control (
  input  [3:0] \function ,
  input  [1:0] ALUOp,
  output [2:0] Operation
);

  and and_1 (Operation[0], ALUOp[1], \function [1]);
  or or_1 (Operation[1], ~\function [2], ~ALUOp[1]);  // OR_Gate
  and and_2 (Operation[2], \function [0], ALUOp[1]);
endmodule
